// Logisim project Projekt.circ as structural Verilog: 6 circuits, main circuit main
module main (
  input  [1:0] OPCode,
  input  [31:0] X,
  input  [31:0] Y,
  output [31:0] Out,
  output [7:0] Status,
  output [3:0] Compare
);

  fpu fpu_1 (.Operation(OPCode), .X(X), .Y(Y), .Out(Out), .Status(Status), .Compare(Compare));
endmodule

module NumInfo (
  input  [31:0] Number,
  output Sign,
  output [7:0] Exponent,
  output [7:0] Addjusted_exponent,
  output [22:0] Mantisa,
  output Normalized,
  output Zero,
  output Inf,
  output NaN
);

  wire E1, M0;
  wire [7:0] subtractor_1_out;

  nor nor_1 (Zero, Normalized, M0);
  and and_1 (Inf, E1, ~M0);  // AND_Gate
  and and_2 (NaN, E1, M0);
  or or_1 (Normalized, Number[23], Number[24], Number[25], Number[26], Number[27], Number[28], Number[29], Number[30]);
  or or_2 (M0, Number[0], Number[1], Number[2], Number[3], Number[4], Number[5], Number[6], Number[7], Number[8], Number[9], Number[10], Number[11], Number[12], Number[13], Number[14], Number[15], Number[16], Number[17], Number[18], Number[19], Number[20], Number[21], Number[22]);
  and and_3 (E1, Number[23], Number[24], Number[25], Number[26], Number[27], Number[28], Number[29], Number[30]);
  Subtractor subtractor_1 (.a(Number[30:23]), .b(8'h7f), .out(subtractor_1_out));  // open: bin, bout
  Multiplexer #(.width(8), .enable("false")) multiplexer_1 (
    .in0(8'h82), .in1(subtractor_1_out), .out(Addjusted_exponent), .sel(Normalized));

  assign Exponent = Number[30:23];
  assign Mantisa = Number[22:0];
  assign Sign = Number[31];

  // Other names for the same wires on the sheet: E0 = Normalized; EA[7:0] = Addjusted_exponent;
  //   M[22:0] = Number[22:0]; E[7:0] = Number[30:23]
endmodule

module Comparator (
  input  [31:0] X,
  input  [31:0] Y,
  output X_Y,
  output X_Y_2,
  output X_Y_3,
  output Unordered
);

  wire and_1_out, and_2_out, and_3_out, numinfo_1_nan, numinfo_1_sign, numinfo_1_zero, numinfo_2_nan,
       numinfo_2_sign, numinfo_2_zero;
  wire [2:0] comparator_1_gt, comparator_2_gt, comparator_3_gt, multiplexer_1_out, multiplexer_2_out,
       multiplexer_3_out;
  wire [7:0] numinfo_1_exponent, numinfo_2_exponent;
  wire [22:0] numinfo_1_mantisa, numinfo_2_mantisa;

  NumInfo numinfo_1 (
    .Number(X), .Sign(numinfo_1_sign), .Mantisa(numinfo_1_mantisa), .Zero(numinfo_1_zero),
    .NaN(numinfo_1_nan), .Exponent(numinfo_1_exponent));  // open: Inf, Normalized, Addjusted_exponent
  NumInfo numinfo_2 (
    .Number(Y), .Sign(numinfo_2_sign), .Mantisa(numinfo_2_mantisa), .Zero(numinfo_2_zero),
    .NaN(numinfo_2_nan), .Exponent(numinfo_2_exponent));  // open: Inf, Normalized, Addjusted_exponent
  and and_1 (and_1_out, numinfo_1_zero, numinfo_2_zero);
  Comparator_part #(.width(1)) comparator_1 (
    .a(numinfo_1_sign), .b(numinfo_2_sign), .gt(comparator_1_gt[0]), .eq(comparator_1_gt[1]),
    .lt(comparator_1_gt[2]));
  Comparator_part #(.mode("unsigned")) comparator_2 (
    .a(numinfo_1_exponent), .b(numinfo_2_exponent), .gt(comparator_2_gt[0]), .eq(comparator_2_gt[1]),
    .lt(comparator_2_gt[2]));
  Comparator_part #(.width(23), .mode("unsigned")) comparator_3 (
    .a(numinfo_1_mantisa), .b(numinfo_2_mantisa), .gt(comparator_3_gt[0]), .eq(comparator_3_gt[1]),
    .lt(comparator_3_gt[2]));
  or or_1 (Unordered, numinfo_1_nan, numinfo_2_nan);
  and and_2 (and_2_out, numinfo_1_sign, numinfo_2_sign);
  Multiplexer #(.width(3), .enable("false")) multiplexer_1 (
    .in0(comparator_2_gt), .in1(comparator_3_gt), .out(multiplexer_1_out), .sel(comparator_2_gt[1]));
  Multiplexer #(.width(3), .enable("false")) multiplexer_2 (
    .in0(comparator_1_gt), .in1(multiplexer_1_out), .out(multiplexer_2_out), .sel(comparator_1_gt[1]));
  Multiplexer #(.width(3), .enable("false")) multiplexer_3 (
    .in0(multiplexer_2_out), .in1(3'b010), .out({multiplexer_3_out[2], X_Y_2, multiplexer_3_out[0]}),
    .sel(and_1_out));
  and and_3 (and_3_out, ~X_Y_2, and_2_out);  // AND_Gate
  xor xor_1 (X_Y, multiplexer_3_out[0], and_3_out);
  xor xor_2 (X_Y_3, multiplexer_3_out[2], and_3_out);

  // Notes on the sheet:
  //   Are both 0?
  //   Sign
  //   Exponent
  //   Mantisa
  //   Is any NaN?
  //   Are both numbers negative?
endmodule

module Adder (
  input  [31:0] X,
  input  [31:0] Y,
  input  Subtract,
  output Underflow,
  output [31:0] Out,
  output Invalid,
  output Overflow
);

  wire adder_1_cout, adder_2_cout, and_2_out, and_4_out, and_6_out, and_7_out, and_8_out, bitfinder_1_found,
       BNN, EO, EQ, ES, nor_2_out, numinfo_1_inf, numinfo_1_nan, numinfo_1_normalized, numinfo_2_inf,
       numinfo_2_nan, numinfo_2_normalized, or_1_out, or_4_out, or_7_out, subtractor_3_bout;
  wire [2:0] comparator_1_gt, comparator_2_gt, multiplexer_1_out;
  wire [4:0] bit_extender_5_out, bit_extender_7_out, bitfinder_1_index, or_2_out, subtractor_2_out;
  wire [7:0] adder_2_out, and_9_out, bit_extender_3_out, bit_extender_9_out, bit_extender_10_out, EE,
       multiplexer_7_out, numinfo_1_addjusted_exponent, numinfo_1_exponent, numinfo_2_addjusted_exponent,
       subtractor_1_out, subtractor_3_out;
  wire [22:0] bit_extender_11_out, bit_extender_12_out, numinfo_1_mantisa, numinfo_2_mantisa;
  wire [23:0] adder_1_out, and_3_out, and_5_out, bit_extender_1_out, bit_extender_2_out, bit_extender_4_out,
       bit_extender_6_out, multiplexer_4_out, multiplexer_5_out, multiplexer_6_out, negator_1_out,
       shifter_1_out, shifter_2_out;
  wire [24:0] bit_extender_8_out;
  wire [31:0] G, S;
  wire [31:31] and_10_out, xor_1_out;

  NumInfo numinfo_1 (
    .Number(G), .Sign(ES), .Mantisa(numinfo_1_mantisa), .Inf(numinfo_1_inf), .NaN(numinfo_1_nan),
    .Normalized(numinfo_1_normalized), .Addjusted_exponent(numinfo_1_addjusted_exponent),
    .Exponent(numinfo_1_exponent));  // open: Zero
  NumInfo numinfo_2 (
    .Number(S), .Mantisa(numinfo_2_mantisa), .Inf(numinfo_2_inf), .NaN(numinfo_2_nan),
    .Normalized(numinfo_2_normalized), .Addjusted_exponent(numinfo_2_addjusted_exponent));  // open: Sign, Zero, Exponent
  xor xor_1 (xor_1_out[31], Subtract, Y[31]);
  assign bit_extender_1_out = {{1{numinfo_1_normalized}}, numinfo_1_mantisa};  // Bit_Extender bit_extender_1
  assign bit_extender_2_out = {{1{numinfo_2_normalized}}, numinfo_2_mantisa};  // Bit_Extender bit_extender_2
  Subtractor subtractor_1 (
    .a(numinfo_1_addjusted_exponent), .b(numinfo_2_addjusted_exponent), .out(subtractor_1_out));  // open: bin, bout
  assign bit_extender_3_out = {{7{EQ}}, EQ};  // Bit_Extender bit_extender_3
  assign EE = bit_extender_3_out & numinfo_1_exponent;  // AND_Gate and_1, 8 bits wide
  nor nor_1 (BNN, numinfo_1_normalized, numinfo_2_normalized);
  assign bit_extender_4_out = {{23{EQ}}, EQ};  // Bit_Extender bit_extender_4
  Bit_Extender #(.out_width(5), .\type ("sign")) bit_extender_5 (.in(subtractor_1_out), .out(bit_extender_5_out));
  and and_2 (and_2_out, numinfo_1_inf, numinfo_2_inf);
  xor xor_2 (EO, X[31], xor_1_out[31]);
  Comparator_part #(.mode("unsigned")) comparator_1 (
    .a(X[30:23]), .b(Y[30:23]), .gt(comparator_1_gt[0]), .eq(comparator_1_gt[1]), .lt(comparator_1_gt[2]));
  Comparator_part #(.width(23), .mode("unsigned")) comparator_2 (
    .a(X[22:0]), .b(Y[22:0]), .gt(comparator_2_gt[0]), .eq(comparator_2_gt[1]), .lt(comparator_2_gt[2]));
  assign bit_extender_6_out = {{23{EQ}}, EQ};  // Bit_Extender bit_extender_6
  assign and_3_out = bit_extender_4_out & bit_extender_2_out;  // AND_Gate and_3, 24 bits wide
  assign bit_extender_7_out = {{4{or_1_out}}, or_1_out};  // Bit_Extender bit_extender_7
  or or_1 (or_1_out, subtractor_1_out[5], subtractor_1_out[6], subtractor_1_out[7]);
  and and_4 (and_4_out, and_2_out, EO);
  Multiplexer #(.width(3), .enable("false")) multiplexer_1 (
    .in0(comparator_1_gt), .in1(comparator_2_gt), .out(multiplexer_1_out), .sel(comparator_1_gt[1]));
  assign and_5_out = bit_extender_6_out & bit_extender_1_out;  // AND_Gate and_5, 24 bits wide
  assign or_2_out = bit_extender_5_out | bit_extender_7_out;  // OR_Gate or_2, 5 bits wide
  or or_3 (Invalid, and_4_out, numinfo_1_nan, numinfo_2_nan);
  Multiplexer #(.width(32), .enable("false")) multiplexer_2 (
    .in0(X), .in1({xor_1_out[31], Y[30:0]}), .out(G), .sel(multiplexer_1_out[2]));
  Multiplexer #(.width(32), .enable("false")) multiplexer_3 (
    .in0({xor_1_out[31], Y[30:0]}), .in1(X), .out(S), .sel(multiplexer_1_out[2]));
  Negator #(.width(24)) negator_1 (.in(shifter_1_out), .out(negator_1_out));
  Shifter #(.width(24), .shift("lr")) shifter_1 (.in(and_3_out), .\dist (or_2_out), .out(shifter_1_out));
  nand nand_1 (EQ, EO, multiplexer_1_out[1]);
  Multiplexer #(.width(24), .enable("false")) multiplexer_4 (
    .in0(shifter_1_out), .in1(negator_1_out), .out(multiplexer_4_out), .sel(EO));
  Adder_part #(.width(24)) adder_1 (
    .a(and_5_out), .b(multiplexer_4_out), .out(adder_1_out), .cout(adder_1_cout));  // open: cin
  and and_6 (and_6_out, adder_1_out[23], BNN);
  and and_7 (and_7_out, ~EO, adder_1_cout);  // AND_Gate
  or or_4 (or_4_out, and_7_out, and_6_out);
  Adder_part adder_2 (.a(EE), .b({8{1'b0}}), .out(adder_2_out), .cin(or_4_out), .cout(adder_2_cout));
  assign bit_extender_8_out = {{1{1'b1}}, adder_1_out};  // Bit_Extender bit_extender_8
  Multiplexer #(.width(24), .enable("false")) multiplexer_5 (
    .in0(adder_1_out), .in1(bit_extender_8_out[24:1]), .out(multiplexer_5_out), .sel(and_7_out));
  and and_8 (and_8_out, adder_2_out[0], adder_2_out[1], adder_2_out[2], adder_2_out[3], adder_2_out[4], adder_2_out[5], adder_2_out[6], adder_2_out[7]);
  BitFinder #(.width(24), .\type ("high1")) bitfinder_1 (
    .in(multiplexer_5_out), .index(bitfinder_1_index), .found(bitfinder_1_found));
  or or_5 (Overflow, and_8_out, adder_2_cout);
  Subtractor #(.width(5)) subtractor_2 (
    .a(5'b10111), .b(bitfinder_1_index), .out(subtractor_2_out));  // open: bin, bout
  assign bit_extender_9_out = {{7{bitfinder_1_found}}, bitfinder_1_found};  // Bit_Extender bit_extender_9
  nor nor_2 (nor_2_out, subtractor_3_out[0], subtractor_3_out[1], subtractor_3_out[2], subtractor_3_out[3], subtractor_3_out[4], subtractor_3_out[5], subtractor_3_out[6], subtractor_3_out[7]);
  Shifter #(.width(24)) shifter_2 (.in(multiplexer_5_out), .\dist (subtractor_2_out), .out(shifter_2_out));
  assign bit_extender_10_out = {{3{1'b0}}, subtractor_2_out};  // Bit_Extender bit_extender_10
  assign and_9_out = bit_extender_10_out & bit_extender_9_out;  // AND_Gate and_9, 8 bits wide
  or or_6 (Underflow, nor_2_out, subtractor_3_bout);
  Multiplexer #(.width(24), .enable("false")) multiplexer_6 (
    .in0(shifter_2_out), .in1(multiplexer_5_out), .out(multiplexer_6_out), .sel(Underflow));
  Subtractor subtractor_3 (
    .a(adder_2_out), .b(and_9_out), .out(subtractor_3_out), .bout(subtractor_3_bout));  // open: bin
  Bit_Extender #(.in_width(24), .out_width(23)) bit_extender_11 (.in(multiplexer_6_out), .out(bit_extender_11_out));
  Multiplexer #(.width(8), .enable("false")) multiplexer_7 (
    .in0(subtractor_3_out), .in1(adder_2_out), .out(multiplexer_7_out), .sel(subtractor_3_bout));
  and and_10 (and_10_out[31], ES, ~Invalid);  // AND_Gate
  assign bit_extender_12_out = {{22{Invalid}}, Invalid};  // Bit_Extender bit_extender_12
  Multiplexer #(.width(32), .enable("false")) multiplexer_8 (
    .in0({ES, multiplexer_7_out, bit_extender_11_out}),
    .in1({and_10_out[31], {8{1'b1}}, bit_extender_12_out}), .out(Out), .sel(or_7_out));
  or or_7 (or_7_out, Invalid, Overflow);

  // Other names for the same wires on the sheet: INV = Invalid
endmodule

module Mult (
  input  [31:0] X,
  input  [31:0] Y,
  output [31:0] Out,
  output Overflow,
  output Underflow,
  output NaN
);

  wire and_1_out, and_2_out, and_3_out, and_4_out, and_5_out, and_6_out, and_7_out, and_8_out, and_9_out,
       and_10_out, and_11_out, and_12_out, and_13_out, and_14_out, and_15_out, and_16_out, and_17_out,
       and_18_out, and_19_out, and_20_out, and_21_out, and_22_out, and_23_out, and_24_out, and_25_out,
       and_26_out, and_28_out, and_29_out, and_30_out, and_31_out, and_32_out, and_34_out, and_35_out,
       and_36_out, and_38_out, and_39_out, and_40_out, and_41_out, comparator_1_gt, comparator_2_lt,
       comparator_3_gt, comparator_4_gt, comparator_5_lt, comparator_6_lt, comparator_21_lt,
       comparator_22_gt, minus_inf, minus_inf_x, minus_inf_y, minus_x, minus_y, minus_zero, minus_zero_x,
       minus_zero_y, NaNx, NaNy, nor_1_out, nor_2_out, nor_3_out, nor_4_out, nor_7_out, not_1_out, not_2_out,
       not_3_out, not_4_out, not_5_out, not_6_out, not_7_out, not_8_out, not_9_out, not_10_out, NZNIX, NZNIY,
       OP, OP_minus, OP_plus, or_5_out, or_6_out, or_10_out, or_11_out, or_12_out, or_13_out, or_14_out,
       or_15_out, or_16_out, or_17_out, plus_inf, plus_inf_x, plus_inf_y, plus_x, plus_y, plus_zero,
       plus_zero_x, plus_zero_y, s0, sub, UP, UP_minus, UP_plus, xn, yn;
  wire [2:0] priority_encoder_1_out;
  wire [4:0] bit_extender_9_out, bit_extender_10_out, bitfinder_1_index, bitfinder_2_index, subtractor_6_out,
       subtractor_7_out;
  wire [7:0] adder_5_out, bias, bit_extender_7_out, multiplexer_3_out, subtractor_5_out;
  wire [8:0] adder_1_out, adder_2_out, bit_extender_1_out, bit_extender_2_out, bit_extender_3_out,
       bit_extender_4_out, ex_ey, multiplexer_1_out, multiplexer_2_out, subtractor_1_out, subtractor_2_out,
       subtractor_3_out, subtractor_4_out;
  wire [22:0] bit_extender_8_out, bit_extender_11_out, bit_extender_12_out, multiplexer_7_out;
  wire [23:0] bit_extender_5_out, bit_extender_6_out, multiplexer_4_out, multiplexer_5_out,
       multiplier_1_cout, shifter_1_out, shifter_2_out, shifter_3_out, shifter_4_out;
  wire [30:0] X_Y;

  // Probe on X
  // Probe on Y
  assign bit_extender_1_out = {{4{1'b0}}, subtractor_6_out};  // Bit_Extender bit_extender_1
  assign bit_extender_2_out = {{4{1'b0}}, subtractor_7_out};  // Bit_Extender bit_extender_2
  Adder_part #(.width(9)) adder_1 (.a(9'h7e), .b(bit_extender_1_out), .out(adder_1_out));  // open: cin, cout
  // Probe on adder_1_out
  Adder_part #(.width(9)) adder_2 (.a(9'h7e), .b(bit_extender_2_out), .out(adder_2_out));  // open: cin, cout
  // Probe on adder_2_out
  and and_1 (and_1_out, minus_x, minus_inf_y);
  and and_2 (and_2_out, minus_x, plus_inf_y);
  // Probe on bit_extender_3_out
  assign bit_extender_3_out = {{1{1'b0}}, X[30:23]};  // Bit_Extender bit_extender_3
  // Probe on bit_extender_4_out
  assign bit_extender_4_out = {{1{1'b0}}, Y[30:23]};  // Bit_Extender bit_extender_4
  Subtractor #(.width(9)) subtractor_1 (.a({9{1'b0}}), .b(adder_1_out), .out(subtractor_1_out));  // open: bin, bout
  // Probe on subtractor_1_out
  Subtractor #(.width(9)) subtractor_2 (.a({9{1'b0}}), .b(adder_2_out), .out(subtractor_2_out));  // open: bin, bout
  // Probe on subtractor_2_out
  and and_3 (and_3_out, plus_inf_x, plus_inf_y);
  and and_4 (and_4_out, plus_inf_x, plus_y);
  and and_5 (and_5_out, minus_inf_x, minus_inf_y);
  and and_6 (and_6_out, minus_inf_x, minus_y);
  and and_7 (and_7_out, plus_x, plus_inf_y);
  and and_8 (and_8_out, plus_inf_x, minus_inf_y);
  and and_9 (and_9_out, plus_inf_x, minus_y);
  and and_10 (and_10_out, minus_inf_x, plus_inf_y);
  and and_11 (and_11_out, minus_inf_x, plus_y);
  and and_12 (and_12_out, plus_x, minus_inf_y);
  Subtractor #(.width(9)) subtractor_3 (.a(bit_extender_3_out), .b(9'h7f), .out(subtractor_3_out));  // open: bin, bout
  Subtractor #(.width(9)) subtractor_4 (.a(bit_extender_4_out), .b(9'h7f), .out(subtractor_4_out));  // open: bin, bout
  assign bit_extender_5_out = {{1{xn}}, X[22:0]};  // Bit_Extender bit_extender_5
  assign bit_extender_6_out = {{1{yn}}, Y[22:0]};  // Bit_Extender bit_extender_6
  // Probe on subtractor_3_out
  // Probe on multiplexer_1_out
  // Probe on multiplexer_2_out
  Multiplexer #(.width(9)) multiplexer_1 (
    .in0(subtractor_1_out), .in1(subtractor_3_out), .out(multiplexer_1_out), .sel(xn));  // open: en
  Adder_part #(.width(9)) adder_3 (.a(multiplexer_1_out), .b(multiplexer_2_out), .out(ex_ey));  // open: cin, cout
  Multiplexer #(.width(9)) multiplexer_2 (
    .in0(subtractor_2_out), .in1(subtractor_4_out), .out(multiplexer_2_out), .sel(yn));  // open: en
  Multiplier #(.width(24)) multiplier_1 (
    .a(multiplexer_4_out), .b(multiplexer_5_out), .cout(multiplier_1_cout));  // open: out, cin
  // Probe on bias
  BitFinder #(.width(24), .\type ("high1")) bitfinder_1 (
    .in(bit_extender_6_out), .index(bitfinder_1_index));  // open: found
  Bit_Extender #(.in_width(9), .out_width(8)) bit_extender_7 (.in(ex_ey), .out(bit_extender_7_out));
  or or_1 (plus_inf, and_3_out, and_4_out, and_5_out, and_6_out, and_7_out, and_1_out);
  or or_2 (minus_inf, and_8_out, and_9_out, and_10_out, and_11_out, and_12_out, and_2_out);
  xor xor_1 (s0, X[31], Y[31]);
  // Probe on bit_extender_7_out
  not not_1 (not_1_out, multiplier_1_cout[23]);
  Subtractor subtractor_5 (.a({8{1'b0}}), .b(bias), .out(subtractor_5_out));  // open: bin, bout
  Subtractor #(.width(5)) subtractor_6 (
    .a(5'b10111), .b(bitfinder_2_index), .out(subtractor_6_out));  // open: bin, bout
  Subtractor #(.width(5)) subtractor_7 (
    .a(5'b10111), .b(bitfinder_1_index), .out(subtractor_7_out));  // open: bin, bout
  // Probe on bias
  Adder_part adder_4 (.a(8'h7f), .b(bit_extender_7_out), .out(bias));  // open: cin, cout
  // Probe on adder_5_out
  Adder_part adder_5 (.a(bit_extender_7_out), .b(8'h80), .out(adder_5_out));  // open: cin, cout
  Bit_Extender #(.in_width(24), .out_width(23)) bit_extender_8 (.in(multiplier_1_cout), .out(bit_extender_8_out));
  assign bit_extender_9_out = {{4{1'b0}}, not_1_out};  // Bit_Extender bit_extender_9
  // Probe on subtractor_5_out
  Shifter #(.width(24)) shifter_1 (.in(bit_extender_5_out), .\dist (subtractor_6_out), .out(shifter_1_out));
  Shifter #(.width(24)) shifter_2 (.in(bit_extender_6_out), .\dist (subtractor_7_out), .out(shifter_2_out));
  // Probe on multiplexer_3_out
  Multiplexer #(.width(8)) multiplexer_3 (
    .in0(bias), .in1(adder_5_out), .out(multiplexer_3_out), .sel(multiplier_1_cout[23]));  // open: en
  Shifter #(.width(24)) shifter_3 (.in(multiplier_1_cout), .\dist (bit_extender_9_out), .out(shifter_3_out));
  Bit_Extender #(.out_width(5)) bit_extender_10 (.in(subtractor_5_out), .out(bit_extender_10_out));
  Bit_Extender #(.in_width(24), .out_width(23)) bit_extender_11 (.in(shifter_3_out), .out(bit_extender_11_out));
  Shifter #(.width(24), .shift("lr")) shifter_4 (
    .in(multiplier_1_cout), .\dist (bit_extender_10_out), .out(shifter_4_out));
  Multiplexer #(.width(24)) multiplexer_4 (
    .in0(shifter_1_out), .in1(bit_extender_5_out), .out(multiplexer_4_out), .sel(xn));  // open: en
  BitFinder #(.width(24), .\type ("high1")) bitfinder_2 (
    .in(bit_extender_5_out), .index(bitfinder_2_index));  // open: found
  Multiplexer #(.width(24)) multiplexer_5 (
    .in0(shifter_2_out), .in1(bit_extender_6_out), .out(multiplexer_5_out), .sel(yn));  // open: en
  and and_13 (and_13_out, minus_x, minus_zero_y);
  and and_14 (and_14_out, plus_zero_x, minus_zero_y);
  and and_15 (and_15_out, plus_zero_x, minus_y);
  and and_16 (and_16_out, minus_zero_x, plus_zero_y);
  and and_17 (and_17_out, minus_zero_x, plus_y);
  and and_18 (and_18_out, plus_x, minus_zero_y);
  and and_19 (and_19_out, minus_x, plus_zero_y);
  Multiplexer #(.width(8)) multiplexer_6 (
    .in0(multiplexer_3_out), .in1({8{1'b0}}), .out(X_Y[30:23]), .sel(sub));  // open: en
  Multiplexer #(.width(23)) multiplexer_7 (
    .in0(bit_extender_8_out), .in1(bit_extender_11_out), .out(multiplexer_7_out), .sel(not_2_out));  // open: en
  not not_2 (not_2_out, multiplier_1_cout[23]);
  // Probe on bit_extender_10_out
  and and_20 (and_20_out, plus_zero_x, plus_zero_y);
  and and_21 (and_21_out, plus_zero_x, plus_y);
  and and_22 (and_22_out, minus_zero_x, minus_zero_y);
  and and_23 (and_23_out, minus_zero_x, minus_y);
  and and_24 (and_24_out, plus_x, plus_zero_y);
  // Probe on {s0, X_Y}
  Multiplexer #(.width(23)) multiplexer_8 (
    .in0(multiplexer_7_out), .in1(bit_extender_12_out), .out(X_Y[22:0]), .sel(sub));  // open: en
  Bit_Extender #(.in_width(24), .out_width(23)) bit_extender_12 (.in(shifter_4_out), .out(bit_extender_12_out));
  // Probe on 9'h80
  not not_3 (not_3_out, NZNIX);
  not not_4 (not_4_out, X[31]);
  not not_5 (not_5_out, NZNIX);
  // Probe on 9'hff
  // Probe on 9'hff
  Comparator_part #(.width(9), .mode("unsigned")) comparator_1 (
    .a(ex_ey), .b(9'h80), .gt(comparator_1_gt));  // open: eq, lt
  nor nor_1 (nor_1_out, X[31], not_3_out);
  nor nor_2 (nor_2_out, not_4_out, not_5_out);
  or or_3 (plus_zero, and_20_out, and_21_out, and_22_out, and_23_out, and_24_out, and_13_out);
  or or_4 (minus_zero, and_14_out, and_15_out, and_16_out, and_17_out, and_18_out, and_19_out);
  Comparator_part #(.width(9), .mode("unsigned")) comparator_2 (
    .a(ex_ey), .b(9'h16b), .lt(comparator_2_lt));  // open: gt, eq
  // Probe on 9'h16b
  Comparator_part #(.width(9), .mode("unsigned")) comparator_3 (
    .a(multiplexer_1_out), .b(9'hff), .gt(comparator_3_gt));  // open: eq, lt
  Comparator_part #(.width(9), .mode("unsigned")) comparator_4 (
    .a(multiplexer_2_out), .b(9'hff), .gt(comparator_4_gt));  // open: eq, lt
  // Probe on 9'h100
  // Probe on 9'h100
  not not_6 (not_6_out, nor_1_out);
  Comparator_part #(.width(9), .mode("unsigned")) comparator_5 (
    .a(multiplexer_2_out), .b(9'h100), .lt(comparator_5_lt));  // open: gt, eq
  Comparator_part #(.width(9), .mode("unsigned")) comparator_6 (
    .a(multiplexer_1_out), .b(9'h100), .lt(comparator_6_lt));  // open: gt, eq
  Comparator_part #(.width(32), .mode("unsigned")) comparator_7 (
    .a(X), .b(32'h7f800000), .eq(plus_inf_x));  // open: gt, lt
  Comparator_part #(.width(32), .mode("unsigned")) comparator_8 (
    .a(X), .b({32{1'b0}}), .eq(plus_zero_x));  // open: gt, lt
  Comparator_part #(.width(32), .mode("unsigned")) comparator_9 (
    .a(X), .b(32'hff800000), .eq(minus_inf_x));  // open: gt, lt
  Comparator_part #(.width(32), .mode("unsigned")) comparator_10 (
    .a(X), .b(32'h80000000), .eq(minus_zero_x));  // open: gt, lt
  Comparator_part #(.width(1), .mode("unsigned")) comparator_11 (.a(not_6_out), .b(1'b0), .eq(plus_x));  // open: gt, lt
  Comparator_part #(.width(1), .mode("unsigned")) comparator_12 (
    .a(nor_2_out), .b(1'b1), .eq(minus_x));  // open: gt, lt
  and and_25 (and_25_out, comparator_3_gt, comparator_4_gt);
  and and_26 (and_26_out, comparator_5_lt, comparator_6_lt);
  nor nor_3 (nor_3_out, Y[31], not_7_out);
  not not_7 (not_7_out, NZNIY);
  not not_8 (not_8_out, Y[31]);
  nor nor_4 (nor_4_out, not_8_out, not_9_out);
  not not_9 (not_9_out, NZNIY);
  or or_5 (or_5_out, NaNx, NaNy);
  and and_27 (OP, comparator_2_lt, and_25_out);
  Comparator_part #(.width(32), .mode("unsigned")) comparator_13 (
    .a(Y), .b(32'h7f800000), .eq(plus_inf_y));  // open: gt, lt
  Comparator_part #(.width(32), .mode("unsigned")) comparator_14 (
    .a(Y), .b({32{1'b0}}), .eq(plus_zero_y));  // open: gt, lt
  Comparator_part #(.width(32), .mode("unsigned")) comparator_15 (
    .a(Y), .b(32'hff800000), .eq(minus_inf_y));  // open: gt, lt
  Comparator_part #(.width(32), .mode("unsigned")) comparator_16 (
    .a(Y), .b(32'h80000000), .eq(minus_zero_y));  // open: gt, lt
  not not_10 (not_10_out, nor_3_out);
  and and_28 (and_28_out, minus_inf_x, minus_zero_y);
  and and_29 (and_29_out, plus_zero_x, plus_inf_y);
  and and_30 (and_30_out, plus_zero_x, minus_inf_y);
  and and_31 (and_31_out, minus_zero_x, plus_inf_y);
  and and_32 (and_32_out, minus_zero_x, minus_inf_y);
  and and_33 (UP, comparator_1_gt, and_26_out);
  Comparator_part #(.width(1), .mode("unsigned")) comparator_17 (
    .a(not_10_out), .b(1'b0), .eq(plus_y));  // open: gt, lt
  Comparator_part #(.width(1), .mode("unsigned")) comparator_18 (
    .a(nor_4_out), .b(1'b1), .eq(minus_y));  // open: gt, lt
  and and_34 (and_34_out, plus_inf_x, plus_zero_y);
  and and_35 (and_35_out, plus_inf_x, minus_zero_y);
  and and_36 (and_36_out, minus_inf_x, plus_zero_y);
  Demultiplexer demultiplexer_1 (.out0(UP_plus), .out1(UP_minus), .in(OP), .sel(s0));  // open: en
  Demultiplexer demultiplexer_2 (.out0(OP_plus), .out1(OP_minus), .in(UP), .sel(s0));  // open: en
  Comparator_part #(.width(32), .mode("unsigned")) comparator_19 (.a(X), .b(32'h7fffffff), .eq(NaNx));  // open: gt, lt
  Comparator_part #(.width(32), .mode("unsigned")) comparator_20 (.a(Y), .b(32'h7fffffff), .eq(NaNy));  // open: gt, lt
  // Probe on ex_ey
  or or_6 (or_6_out, and_34_out, and_35_out, and_36_out, and_28_out, and_29_out, and_30_out, and_31_out, and_32_out);
  or or_7 (yn, Y[23], Y[24], Y[25], Y[26], Y[27], Y[28], Y[29], Y[30]);
  Comparator_part #(.width(9), .mode("unsigned")) comparator_21 (
    .a(ex_ey), .b(9'h182), .lt(comparator_21_lt));  // open: gt, eq
  Comparator_part #(.width(9), .mode("unsigned")) comparator_22 (
    .a(ex_ey), .b(9'h16a), .gt(comparator_22_gt));  // open: eq, lt
  nor nor_5 (NZNIX, plus_inf_x, plus_zero_x, minus_inf_x, minus_zero_x, NaNx);
  nor nor_6 (NZNIY, plus_inf_y, plus_zero_y, minus_inf_y, minus_zero_y, NaNy);
  or or_8 (xn, X[23], X[24], X[25], X[26], X[27], X[28], X[29], X[30]);
  or or_9 (NaN, or_5_out, or_6_out);
  and and_37 (sub, comparator_21_lt, comparator_22_gt);
  // Probe on {s0, X_Y}
  nor nor_7 (nor_7_out, plus_inf, plus_zero, NaN, minus_inf, minus_zero);
  and and_38 (and_38_out, nor_7_out, OP_plus);
  and and_39 (and_39_out, nor_7_out, UP_plus);
  and and_40 (and_40_out, nor_7_out, OP_minus);
  and and_41 (and_41_out, nor_7_out, UP_minus);
  or or_10 (or_10_out, plus_inf, and_38_out);
  or or_11 (or_11_out, plus_zero, and_39_out);
  or or_12 (or_12_out, minus_inf, and_40_out);
  or or_13 (or_13_out, minus_zero, and_41_out);
  Multiplexer #(.select(3), .width(32)) multiplexer_9 (
    .in0({s0, X_Y}), .in1(32'h7f800000), .in2({32{1'b0}}), .in3(32'h7fffffff), .in4(32'hff800000),
    .in5(32'h80000000), .out(Out), .sel(priority_encoder_1_out));  // open: in6, in7, en
  Priority_Encoder priority_encoder_1 (
    .in0(nor_7_out), .in1(or_10_out), .in2(or_11_out), .in3(NaN), .in4(or_12_out), .in5(or_13_out),
    .out(priority_encoder_1_out));  // open: in6, in7, en_in, gs, en_out
  or or_14 (or_14_out, plus_inf, and_38_out);
  or or_15 (or_15_out, plus_zero, and_39_out);
  or or_16 (or_16_out, minus_inf, and_40_out);
  or or_17 (or_17_out, minus_zero, and_41_out);
  // Probe on Out
  or or_18 (Overflow, or_14_out, or_16_out);
  or or_19 (Underflow, or_15_out, or_17_out);

  // Other names for the same wires on the sheet: ex[7:0] = X[30:23]; Sx = X[31]; X_Y[31] = s0; X_Y_out[31:0] = Out;
  //   ey[7:0] = Y[30:23]; Sy = Y[31]

  // Notes on the sheet:
  //   pre_lzc
  //   pre_lzc
  //   126
  //   126
  //   PLUS INIFNITY
  //   MINUS INFINITY
  //   PLUS INFNITY
  //   MINUS INFINITY
  //   xe + ye b + 1
  //   SHIFTER
  //   PLUS ZERO
  //   PLUS ZERO
  //   MINUS ZERO
  //   +i X
  //   + 0 X
  //   -i X
  //   -0 X
  //   +x
  //   -x
  //   OVERFLOW/UNDERFLOW
  //   +i Y
  //   + 0 Y
  //   -i Y
  //   -0 Y
  //   +y
  //   -y
  //   +0
  //   -0
  //   +i
  //   -i
  //   16a hex is 362 decimal = -150 in signed decila for 9 bits
  //   182 hex is 386 decimal = -126 in signed decimal for 9 bits
  //   subnormal ex =0
  //   normal ey = 1
  //   subnormal ey = 0
  //   subnormal = 1
  //   normal ex = 1
  //   norma = 0
  //   minus inf 
  //   minus zero
  //   plus inf x
  //   plus zero 
  //   NaN
endmodule

module fpu (
  input  [1:0] Operation,
  input  [31:0] X,
  input  [31:0] Y,
  output [31:0] Out,
  output [7:0] Status,
  output [3:0] Compare
);

  wire [2:0] adder_1_invalid, mult_1_nan;
  wire [31:0] adder_1_out, mult_1_out;

  Adder adder_1 (
    .X(X), .Out(adder_1_out), .Y(Y), .Invalid(adder_1_invalid[0]), .Subtract(Operation[0]),
    .Overflow(adder_1_invalid[1]), .Underflow(adder_1_invalid[2]));
  Mult mult_1 (
    .X(X), .Y(Y), .Out(mult_1_out), .Overflow(mult_1_nan[1]), .Underflow(mult_1_nan[2]), .NaN(mult_1_nan[0]));
  Comparator comparator_1 (
    .X(X), .Y(Y), .X_Y(Compare[0]), .X_Y_2(Compare[1]), .X_Y_3(Compare[2]), .Unordered(Compare[3]));
  Multiplexer #(.select(2), .width(32), .enable("false")) multiplexer_1 (
    .in0(adder_1_out), .in1(adder_1_out), .in2(mult_1_out), .out(Out), .sel(Operation));  // open: in3
  NumInfo numinfo_1 (
    .Number(Out), .Sign(Status[0]), .Zero(Status[2]), .Inf(Status[3]), .NaN(Status[4]), .Normalized(Status[1]));  // open: Mantisa, Addjusted_exponent, Exponent
  Multiplexer #(.select(2), .width(3), .enable("false")) multiplexer_2 (
    .in0(adder_1_invalid), .in1(adder_1_invalid), .in2(mult_1_nan), .out(Status[7:5]), .sel(Operation));  // open: in3

  // Notes on the sheet:
  //   Legenda:
  //   0 - Dodawanie
  //   1 - Odejmowanie
  //   2 - Mnożenie
  //   3 - Brak
  //   Legenda:
  //   6 - Overflow
  //   7 - Underflow
  //   Legenda:
  //   0 - X większy
  //   1- Równe
  //   2 - Y większy
  //   0 - Czy wynik jest dodatni
  //   1 - Wynik znormalizowany
  //   2 - Wynik jest zerem
  //   3 - Wynik jest INF
  //   4 - Wynik jest NaN
  //   5 - Operacja niepoprawna
  //   4 - Nie można porównać
endmodule
